// Logisim project traffic_light_david.circ as structural Verilog: 1 circuit, main circuit main
module main (
  input  S_N,
  input  S_S,
  input  S_E,
  input  S_W,
  input  P_N,
  input  P_S,
  input  P_E,
  input  P_W,
  output P_N_SIGNAL,
  output P_S_SIGNAL,
  output P_E_SIGNAL,
  output P_N_SIGNAL_2
);

  wire AND1_out, AND2_out, AND3_out, AND4_out, AND5_out, AND_CLOCK_out, clock_out, decoder_1_out0,
       decoder_1_out1, decoder_1_out2, decoder_1_out3, MAJORITY_out, NOT_PE_out, NOT_PN_out, NOT_PS_out,
       NOT_PW_out, OR_EWR_out, OR_NSR_out;
  wire [1:0] COUNTER_q;

  not NOT_PS (NOT_PS_out, P_S);
  not NOT_PN (NOT_PN_out, P_N);
  not NOT_PW (NOT_PW_out, P_W);
  not NOT_PE (NOT_PE_out, P_E);
  and AND1 (AND1_out, S_N, S_S, S_E);
  and AND2 (AND2_out, S_N, S_S, S_W);
  and AND3 (AND3_out, S_N, S_E, S_W);
  and AND4 (AND4_out, S_S, S_E, S_W);
  and AND5 (AND5_out, S_N, S_S, S_E, S_W);
  and and_1 (P_N_SIGNAL, P_N, decoder_1_out2, NOT_PS_out);
  and and_2 (P_S_SIGNAL, P_S, decoder_1_out2, NOT_PN_out);
  and and_3 (P_E_SIGNAL, P_E, decoder_1_out0, NOT_PW_out);
  and and_4 (P_N_SIGNAL_2, P_W, decoder_1_out0, NOT_PE_out);
  or MAJORITY (MAJORITY_out, AND1_out, AND2_out, AND3_out, AND4_out, AND5_out);
  Counter #(.width(2), .max('h3)) COUNTER (
    .Q(COUNTER_q), .clk(AND_CLOCK_out), .clr(1'b0));  // open: load, D, count, carry
  Clock clock (.out(clock_out));
  and AND_CLOCK (AND_CLOCK_out, clock_out, MAJORITY_out);
  Decoder #(.select(2), .enable("false")) decoder_1 (
    .out0(decoder_1_out0), .out1(decoder_1_out1), .out2(decoder_1_out2), .out3(decoder_1_out3),
    .sel(COUNTER_q));
  or OR_NSR (OR_NSR_out, decoder_1_out2, decoder_1_out3);
  or OR_EWR (OR_EWR_out, decoder_1_out0, decoder_1_out1);
  LED NG (.in(decoder_1_out0));
  LED NY (.in(decoder_1_out1));
  LED NR (.in(OR_NSR_out));
  LED SG (.in(decoder_1_out0));
  LED SY (.in(decoder_1_out1));
  LED SR (.in(OR_NSR_out));
  LED EG (.in(decoder_1_out2));
  LED EY (.in(decoder_1_out3));
  LED ER (.in(OR_EWR_out));
  LED WG (.in(decoder_1_out2));
  LED WY (.in(decoder_1_out3));
  LED WR (.in(OR_EWR_out));

  // Notes on the sheet:
  //   3 + SENSORS ACTIVE
  //   NORTH GREEN
  //   NORTH YELLOW
  //   NORTH RED
  //   SOUTH GREEN
  //   SOUTH YELLOW
  //   SOUTH RED
  //   EAST GREEN
  //   EAST YELLOW
  //   EAST RED
  //   WEST GREEN
  //   WEST YELLOW
  //   WEST RED
endmodule
